# Fritzing sketch circuit (saved by Fritzing 0.9.3b)
breadboards: 1

parts:
  Digispark1 = Digispark
  M1 = fc-51 [package=THT]
  U1 = L9110 H-bridge module [part_number="L9110 H-bridge"]
  BATT1 = 3xAAA Switchable Battery Pack w/Bare Wire
  M2 = DC Motor  # not connected
  M3 = DC Motor  # not connected
  R1 = Resistor [tolerance=±5% resistance=10 package=THT]
  R2 = Resistor [tolerance=±5% resistance=10 package=THT]
  R3 = Resistor [tolerance=±5% resistance=10 package=THT]
  R4 = Resistor [tolerance=±5% resistance=10 package=THT]
  BATT2 = 3xAAA Switchable Battery Pack w/Bare Wire  # not connected

nets:
  VIN: Digispark1.VIN, U1.VCC, BATT1.POS
  N1: Digispark1.P0, U1.A-IB
  N2: Digispark1.P1, U1.A-IA
  N3: Digispark1.P2, U1.B-IA
  N4: Digispark1.P3, U1.B-IB
  N5: Digispark1.P4, M1.pin1
  N6: M1.pin2, U1.GND, BATT1.NEG
  N7: U1.MOTOR_A-A, R3.Pin_1
  N8: U1.MOTOR_A-B, R4.Pin_1
  N9: U1.MOTOR_B-A, R2.Pin_0
  N10: U1.MOTOR_B-B, R1.Pin_0

notes:
  AAA Battery pack provides power for all components!
  Black == GND
  This is a shared GND between all devices.
  Here we split the GND (black) and Vcc (red) into three. Giving each component access to power.

custom parts:
  Digispark: The Digispark is an Attiny85 based microcontroller development board similar to the Arduino line, only cheaper, smaller, and a bit less powerful. With a whole host of shields to extend its functionality and the ability to use the familiar Arduino IDE the Digispark is a great way to jump into electronics, or perfect for when an Arduino is too big or too much.
  3xAAA Switchable Battery Pack w/Bare Wire: 3xAAA Switchable Battery Pack w/Bare Wire Connectors
